# Fritzing sketch 100x Non-Inv Amp (saved by Fritzing 0.9.3b)
breadboards: 1

parts:
  VCC1 = Battery block 9V
  R1 = Resistor [tolerance=±5% resistance=10k package=THT]
  R2 = Resistor [tolerance=±5% resistance=100 package=THT]
  R3 = Rotary Potentiometer (Small) [maximum_resistance=100kΩ package=THT]
  IC1 = Dual Op-Amp [package=dip08]
  C1 = Ceramic Capacitor [capacitance=100nF package="100 mil [THT, multilayer]"]
  R4 = Resistor [tolerance=±5% resistance=10k package=THT]
  R5 = Resistor [tolerance=±5% resistance=100 package=THT]

nets:
  N1: VCC1.-, R2.Pin_1, R3.leg1, IC1.A_V-, IC1.B_+IN, C1.0, R5.Pin_1
  N2: VCC1.+, R3.leg2, IC1.A_V+, C1.1
  N3: R1.Pin_0, R3.wiper
  N4: R1.Pin_1, R2.Pin_0, IC1.A_+IN
  N5: IC1.A_OUT, R4.Pin_0
  N6: IC1.A_-IN, R4.Pin_1, R5.Pin_0
  N7: IC1.B_-IN, IC1.B_OUT

notes:
  OUT
  IN
  IN/100
